// Logisim project DDS-T12_1.circ as structural Verilog: 7 circuits, main circuit main
module main (
  input  D1,
  input  D2,
  input  D3,
  input  D4,
  input  D5,
  input  D6,
  input  D7,
  input  CANDIDATE,
  input  LOAD,
  input  CLEAR,
  input  ENABLE,
  output [3:0] out_12,
  output [7:0] out_13,
  output [7:0] out_14,
  output [7:0] out_15,
  output [7:0] out_16,
  output [7:0] out_17,
  output [7:0] out_18,
  output [7:0] out_19
);

  wire clock_1_out, or_1_out, or_2_out, or_3_out, STORE_out;
  wire [2:0] and_3_out, counter_1_count, register_2_q, subtractor_1_out;
  wire [3:0] comparator_1_max_1, comparator_1_max_2, comparator_1_max_3;
  wire [7:0] register_1_dummy;

  score_calculator score_calculator_1 (
    .Score(1'b1), .D1(D1), .D2(D2), .D3(D3), .D4(D4), .B3(out_12[3]), .B2(out_12[2]), .B1(out_12[1]),
    .B0(out_12[0]));
  or or_1 (or_1_out, D7, D6, D5, D4);
  or or_2 (or_2_out, D7, D6, D3, D2);
  or or_3 (or_3_out, D7, D5, D3, D1);
  Register register_1 (
    .counter({1'b0, subtractor_1_out}), .score(out_12), .Enable(clock_1_out), .Dummy(register_1_dummy),
    .Clear(CLEAR), .r1(out_13), .r2(out_14), .r3(out_15), .r4(out_16), .r5(out_17), .r6(out_18), .r7(out_19));  // open: out_6, out_8, out_10, out_12, out_14, out_16, out_18, out_20
  and and_1 (and_3_out[2], CANDIDATE, or_1_out);
  and and_2 (and_3_out[1], CANDIDATE, or_2_out);
  and and_3 (and_3_out[0], CANDIDATE, or_3_out);
  comparator comparator_1 (
    .Token1(out_13), .Token2(out_14), .Token3(out_15), .Token4(out_16), .Token5(out_17), .Token6(out_18),
    .Token7(out_19), .Max_3(comparator_1_max_3), .Max_2(comparator_1_max_2), .Max_1(comparator_1_max_1));
  Hex_Digit_Display hex_digit_display_1 (.value(comparator_1_max_1));  // open: dp
  Clock clock_1 (.out(clock_1_out));
  Hex_Digit_Display hex_digit_display_2 (.value(register_1_dummy[7:4]));  // open: dp
  Hex_Digit_Display hex_digit_display_3 (.value(comparator_1_max_2));  // open: dp
  Counter counter_1 (
    .Enable(ENABLE), .CLK(clock_1_out), .Clear(CLEAR), .Load(LOAD), .B2(and_3_out[2]), .B1(and_3_out[1]),
    .B0(and_3_out[0]), .Count(counter_1_count));  // open: w
  Hex_Digit_Display hex_digit_display_4 (.value(comparator_1_max_3));  // open: dp
  Button STORE (.out(STORE_out));
  Register_part #(.width(3)) register_2 (.D(and_3_out), .en(1'b1), .Q(register_2_q), .clk(STORE_out), .clr(1'b0));
  Subtractor #(.width(3)) subtractor_1 (
    .a(register_2_q), .b(counter_1_count), .out(subtractor_1_out), .bin(1'b0));  // open: bout

  // Notes on the sheet:
  //   Team number : S2-T12
  //   Parishasa K Reddy , 231CS239
  //   R Sairam , 231CS245
  //   Rishi Ramesh, 231CS248
  //   Score calculates the total
  //   score of each candidate
  //   INPUTS
  //   turn this on to input the
  //   number of candidates
  //   MAIN CIRCUIT
  //   comparator compares the scores 
  //   and selects the top 3 candidates
  //   CLK(COUNTER)
  //   Seat 1
  //   OUTPUTS
  //   Seat 2
  //   Seat 3
  //   At first displays the total number of candidates
  //   then it displays the number of candidates applied
  //   Each display showing token number
  //   (candidate number) alloted to
  //   respective seats
  //   Token generation 
  //   Where D1=senior citizen
  //   D2=Disabled
  //   D3=Health patient
  //   D4=Government Official
  //   Instructions
  //   1. Turn on candidate switch to take no. of candidates as input.
  //   3. Click store button to store the no. of candidates
  //   4.Turn off candidate switch and turn on enable switch
  //   5. Now enter the catergories each candidate belong to 
  //   6. For each person u enter give clock pulse to store them
  //   7. You can see the token numbers in the output 
  //   2. Turn on load button and give a clock pulse to activate the counter
endmodule

// score
module score_calculator (
  input  Score,
  input  D1,
  input  D2,
  input  D3,
  input  D4,
  output B3,
  output B2,
  output B1,
  output B0
);

  wire and_1_out, and_2_out, and_3_out, and_4_out, and_5_out, and_6_out, and_7_out, and_8_out, and_9_out,
       not_1_out, not_2_out, not_3_out, not_4_out, or_1_out, or_2_out, or_3_out, xnor_1_out;

  not not_1 (not_1_out, D1);
  not not_2 (not_2_out, D2);
  not not_3 (not_3_out, D3);
  not not_4 (not_4_out, D4);
  and and_1 (and_1_out, D1, D2, D4);
  and and_2 (and_2_out, D3, D4);
  and and_3 (and_3_out, D3, not_4_out);
  and and_4 (and_4_out, not_1_out, not_3_out, D4);
  and and_5 (and_5_out, not_2_out, not_3_out, D4);
  and and_6 (and_6_out, D1, D2, not_4_out);
  and and_7 (and_7_out, not_1_out, D2);
  and and_8 (and_8_out, D2, D3);
  and and_9 (and_9_out, D1, not_2_out, not_3_out);
  or or_1 (or_1_out, and_1_out, and_2_out);
  or or_2 (or_2_out, and_3_out, and_4_out, and_5_out, and_6_out);
  or or_3 (or_3_out, and_7_out, and_8_out, and_9_out);
  xnor xnor_1 (xnor_1_out, D1, D3);
  and and_10 (B3, Score, or_1_out);
  and and_11 (B2, Score, or_2_out);
  and and_12 (B1, Score, or_3_out);
  and and_13 (B0, Score, xnor_1_out);

  // Notes on the sheet:
  //   SCORE CALCULATION
endmodule

module Counter (
  input  Enable,
  input  CLK,
  input  Clear,
  input  Load,
  input  B2,
  input  B1,
  input  B0,
  output [2:0] Count,
  output [2:0] w
);

  Subtractor #(.width(3)) subtractor_1 (.a({B2, B1, B0}), .b(3'b001), .out(w));  // open: bin, bout
  Counter_part #(.width(3), .max('h7), .ongoal("stay")) counter_1 (
    .load(Load), .D(w), .count(Enable), .Q(Count), .clk(CLK), .clr(Clear));  // open: carry
endmodule

// Comparator
module comparator (
  input  [7:0] Token1,
  input  [7:0] Token2,
  input  [7:0] Token3,
  input  [7:0] Token4,
  input  [7:0] Token5,
  input  [7:0] Token6,
  input  [7:0] Token7,
  output [3:0] Max_3,
  output [3:0] Max_2,
  output [3:0] Max_1
);

  wire [3:0] bn2_17_max, bn2_18_max, bn2_18_min;
  wire [7:0] bn1_1_max, bn1_1_min, bn1_2_max, bn1_2_min, bn1_3_max, bn1_3_min, bn1_4_max, bn1_4_min,
       bn1_5_max, bn1_5_min, bn1_6_max, bn1_6_min, bn2_1_max, bn2_1_min, bn2_2_max, bn2_2_min, bn2_3_max,
       bn2_3_min, bn2_4_max, bn2_4_min, bn2_5_max, bn2_5_min, bn2_6_max, bn2_6_min, bn2_7_max, bn2_7_min,
       bn2_8_max, bn2_8_min, bn2_9_max, bn2_9_min, bn2_10_max, bn2_10_min, bn2_11_max, bn2_11_min,
       bn2_12_max, bn2_12_min, bn2_13_max, bn2_13_min, bn2_14_max, bn2_14_min;

  BN2 bn2_1 (.Input_1({8{1'b0}}), .Input_2(Token1), .MIN(bn2_1_min), .MAX(bn2_1_max));
  BN1 bn1_1 (.Input_1(Token2), .Input_2(Token3), .MAX(bn1_1_max), .MIN(bn1_1_min));
  BN2 bn2_2 (.Input_1(Token4), .Input_2(Token5), .MIN(bn2_2_min), .MAX(bn2_2_max));
  BN1 bn1_2 (.Input_1(Token6), .Input_2(Token7), .MAX(bn1_2_max), .MIN(bn1_2_min));
  BN2 bn2_3 (.Input_1(bn2_1_min), .Input_2(bn1_1_max), .MIN(bn2_3_min), .MAX(bn2_3_max));
  BN2 bn2_4 (.Input_1(bn2_1_max), .Input_2(bn1_1_min), .MIN(bn2_4_min), .MAX(bn2_4_max));
  BN1 bn1_3 (.Input_1(bn2_2_min), .Input_2(bn1_2_max), .MAX(bn1_3_max), .MIN(bn1_3_min));
  BN1 bn1_4 (.Input_1(bn2_2_max), .Input_2(bn1_2_min), .MAX(bn1_4_max), .MIN(bn1_4_min));
  BN2 bn2_5 (.Input_1(bn2_3_min), .Input_2(bn2_4_min), .MIN(bn2_5_min), .MAX(bn2_5_max));
  BN2 bn2_6 (.Input_1(bn2_3_max), .Input_2(bn2_4_max), .MIN(bn2_6_min), .MAX(bn2_6_max));
  BN1 bn1_5 (.Input_1(bn1_3_max), .Input_2(bn1_4_max), .MAX(bn1_5_max), .MIN(bn1_5_min));
  BN1 bn1_6 (.Input_1(bn1_3_min), .Input_2(bn1_4_min), .MAX(bn1_6_max), .MIN(bn1_6_min));
  BN2 bn2_7 (.Input_1(bn2_5_min), .Input_2(bn1_5_max), .MIN(bn2_7_min), .MAX(bn2_7_max));
  BN2 bn2_8 (.Input_1(bn2_5_max), .Input_2(bn1_5_min), .MIN(bn2_8_min), .MAX(bn2_8_max));
  BN2 bn2_9 (.Input_1(bn2_6_min), .Input_2(bn1_6_max), .MIN(bn2_9_min), .MAX(bn2_9_max));
  BN2 bn2_10 (.Input_1(bn2_6_max), .Input_2(bn1_6_min), .MIN(bn2_10_min), .MAX(bn2_10_max));
  BN2 bn2_11 (.Input_1(bn2_7_min), .Input_2(bn2_9_min), .MIN(bn2_11_min), .MAX(bn2_11_max));
  BN2 bn2_12 (.Input_1(bn2_8_min), .Input_2(bn2_10_min), .MIN(bn2_12_min), .MAX(bn2_12_max));
  BN2 bn2_13 (.Input_1(bn2_7_max), .Input_2(bn2_9_max), .MIN(bn2_13_min), .MAX(bn2_13_max));
  BN2 bn2_14 (.Input_1(bn2_8_max), .Input_2(bn2_10_max), .MIN(bn2_14_min), .MAX(bn2_14_max));
  BN2 bn2_15 (.Input_1(bn2_11_min), .Input_2(bn2_12_min));  // open: MIN, MAX
  BN2 bn2_16 (.Input_1(bn2_11_max), .Input_2(bn2_12_max));  // open: MIN, MAX
  BN2 bn2_17 (.Input_1(bn2_13_min), .Input_2(bn2_14_min), .MAX({Max_3, bn2_17_max}));  // open: MIN
  BN2 bn2_18 (.Input_1(bn2_13_max), .Input_2(bn2_14_max), .MIN({Max_2, bn2_18_min}), .MAX({Max_1, bn2_18_max}));

  // Notes on the sheet:
  //   SORTING CIRCUIT
endmodule

module Register (
  input  [3:0] counter,
  input  Clear,
  input  [3:0] score,
  input  Enable,
  output [7:0] Dummy,
  output [7:0] out_6,
  output [7:0] r1,
  output [7:0] out_8,
  output [7:0] r2,
  output [7:0] out_10,
  output [7:0] r3,
  output [7:0] out_12,
  output [7:0] r4,
  output [7:0] out_14,
  output [7:0] r5,
  output [7:0] out_16,
  output [7:0] r6,
  output [7:0] out_18,
  output [7:0] r7,
  output [7:0] out_20
);

  wire comparator_1_eq, comparator_2_eq, comparator_3_eq, comparator_4_eq, comparator_5_eq, comparator_6_eq,
       comparator_7_eq;

  Comparator #(.width(4)) comparator_1 (.a(counter), .b(4'b0001), .eq(comparator_1_eq));  // open: gt, lt
  Comparator #(.width(4)) comparator_2 (.a(counter), .b(4'b0010), .eq(comparator_2_eq));  // open: gt, lt
  Comparator #(.width(4)) comparator_3 (.a(counter), .b(4'b0011), .eq(comparator_3_eq));  // open: gt, lt
  Comparator #(.width(4)) comparator_4 (.a(counter), .b(4'b0100), .eq(comparator_4_eq));  // open: gt, lt
  Comparator #(.width(4)) comparator_5 (.a(counter), .b(4'b0101), .eq(comparator_5_eq));  // open: gt, lt
  Comparator #(.width(4)) comparator_6 (.a(counter), .b(4'b0110), .eq(comparator_6_eq));  // open: gt, lt
  Comparator #(.width(4)) comparator_7 (.a(counter), .b(4'b0111), .eq(comparator_7_eq));  // open: gt, lt
  Register_part register_1 (.D({counter, score}), .en(1'b1), .Q(Dummy), .clk(Enable), .clr(Clear));
  Register_part register_2 (.D({counter, score}), .en(comparator_1_eq), .Q(r1), .clk(Enable), .clr(Clear));
  Register_part register_3 (.D({counter, score}), .en(comparator_2_eq), .Q(r2), .clk(Enable), .clr(Clear));
  Register_part register_4 (.D({counter, score}), .en(comparator_3_eq), .Q(r3), .clk(Enable), .clr(Clear));
  Register_part register_5 (.D({counter, score}), .en(comparator_4_eq), .Q(r4), .clk(Enable), .clr(Clear));
  Register_part register_6 (.D({counter, score}), .en(comparator_5_eq), .Q(r5), .clk(Enable), .clr(Clear));
  Register_part register_7 (.D({counter, score}), .en(comparator_6_eq), .Q(r6), .clk(Enable), .clr(Clear));
  Register_part register_8 (.D({counter, score}), .en(comparator_7_eq), .Q(r7), .clk(Enable), .clr(Clear));

  assign out_6 = {counter, score};
  assign out_8 = {counter, score};
  assign out_10 = {counter, score};
  assign out_12 = {counter, score};
  assign out_14 = {counter, score};
  assign out_16 = {counter, score};
  assign out_18 = {counter, score};
  assign out_20 = {counter, score};

  // Notes on the sheet:
  //   Storing Token and Score for each Candidate in Registers
endmodule

module BN1 (
  input  [7:0] Input_1,
  input  [7:0] Input_2,
  output [7:0] MAX,
  output [7:0] MIN
);

  wire and_1_out, comparator_1_lt, comparator_2_eq, comparator_2_gt, multiplexer_3_out, not_1_out, not_2_out,
       not_3_out;
  wire [4:0] bit_extender_1_out, bit_extender_2_out, bit_extender_3_out, bit_extender_4_out;

  assign bit_extender_1_out = {{1{1'b0}}, Input_1[7:4]};  // Bit_Extender bit_extender_1
  assign bit_extender_2_out = {{1{1'b0}}, Input_2[7:4]};  // Bit_Extender bit_extender_2
  assign bit_extender_3_out = {{1{1'b0}}, Input_1[3:0]};  // Bit_Extender bit_extender_3
  assign bit_extender_4_out = {{1{1'b0}}, Input_2[3:0]};  // Bit_Extender bit_extender_4
  Comparator #(.width(5)) comparator_1 (
    .a(bit_extender_1_out), .b(bit_extender_2_out), .lt(comparator_1_lt));  // open: gt, eq
  Comparator #(.width(5)) comparator_2 (
    .a(bit_extender_3_out), .b(bit_extender_4_out), .gt(comparator_2_gt), .eq(comparator_2_eq));  // open: lt
  buf and_1 (and_1_out, comparator_1_lt);  // AND_Gate
  Multiplexer #(.width(8)) multiplexer_1 (.in0(Input_2), .in1(Input_1), .out(MIN), .sel(multiplexer_3_out), .en(1'b1));
  Multiplexer #(.width(8)) multiplexer_2 (.in0(Input_1), .in1(Input_2), .out(MAX), .sel(multiplexer_3_out), .en(1'b1));
  not not_1 (not_1_out, comparator_2_gt);
  not not_2 (not_2_out, comparator_2_eq);
  not not_3 (not_3_out, and_1_out);
  Multiplexer multiplexer_3 (.in0(not_3_out), .in1(not_1_out), .out(multiplexer_3_out), .sel(not_2_out), .en(1'b1));

  // Notes on the sheet:
  //   BITONIC COMPARATOR 1
endmodule

module BN2 (
  input  [7:0] Input_1,
  input  [7:0] Input_2,
  output [7:0] MIN,
  output [7:0] MAX
);

  wire and_1_out, comparator_1_lt, comparator_2_eq, comparator_2_gt, multiplexer_3_out, not_1_out, not_2_out,
       not_3_out;
  wire [4:0] bit_extender_1_out, bit_extender_2_out, bit_extender_3_out, bit_extender_4_out;

  assign bit_extender_1_out = {{1{1'b0}}, Input_1[7:4]};  // Bit_Extender bit_extender_1
  assign bit_extender_2_out = {{1{1'b0}}, Input_2[7:4]};  // Bit_Extender bit_extender_2
  assign bit_extender_3_out = {{1{1'b0}}, Input_1[3:0]};  // Bit_Extender bit_extender_3
  assign bit_extender_4_out = {{1{1'b0}}, Input_2[3:0]};  // Bit_Extender bit_extender_4
  Comparator #(.width(5)) comparator_1 (
    .a(bit_extender_1_out), .b(bit_extender_2_out), .lt(comparator_1_lt));  // open: gt, eq
  Comparator #(.width(5)) comparator_2 (
    .a(bit_extender_3_out), .b(bit_extender_4_out), .gt(comparator_2_gt), .eq(comparator_2_eq));  // open: lt
  buf and_1 (and_1_out, comparator_1_lt);  // AND_Gate
  Multiplexer #(.width(8)) multiplexer_1 (.in0(Input_2), .in1(Input_1), .out(MIN), .sel(multiplexer_3_out), .en(1'b1));
  Multiplexer #(.width(8)) multiplexer_2 (.in0(Input_1), .in1(Input_2), .out(MAX), .sel(multiplexer_3_out), .en(1'b1));
  not not_1 (not_1_out, comparator_2_gt);
  not not_2 (not_2_out, comparator_2_eq);
  not not_3 (not_3_out, and_1_out);
  Multiplexer multiplexer_3 (.in0(not_3_out), .in1(not_1_out), .out(multiplexer_3_out), .sel(not_2_out), .en(1'b1));

  // Notes on the sheet:
  //   BITONIC COMPARATOR 2
endmodule
